# Fritzing sketch AnalogTrigger (saved by Fritzing 0.9.0b)
circuit board: 5.85cm x 2.55cm
breadboards: 1

parts:
  ZENER_5_1V = Zener Diode [part_number=1N4732A breakdown_voltage=3.6V package="300 mil [THT]"]
  COMP = LM 358 Dual Op-Amp [package="DIP8 [THT]"]
  R_1M = Resistor [tolerance=±5% resistance=1M package=THT]
  J1 = female pin header, 2 pins [form="♀ (female)"]
  TRIGGER = LED - 3mm [color="Red (633nm)" package="3 mm [THT]"]
  J2 = shrouded pin header, 6 pins [form="♂ (shrouded male)"]

nets (from the pcb view):
  N1: ZENER_5_1V.cathode, COMP.connector2, R_1M.Pin_0, J1.pin2
  N2: ZENER_5_1V.anode, COMP.connector3, R_1M.Pin_1, J1.pin1, TRIGGER.cathode, J2.pin1
  N3: COMP.connector0, TRIGGER.anode, J2.pin4
  N4: COMP.connector1, J2.pin5
  N5: COMP.connector7, J2.pin6

notes:
  COMP
  VCC
  REF
  SIG
  -
  +
  TRIGGER
  SENSOR
  BUS
  *
  rev #01
