# Fritzing sketch BusBoard (saved by Fritzing 0.9.0b)
circuit board: 32.3106cm x 5cm
breadboards: 1

parts:
  PI = shrouded pin header, 40 pins [form="♂ (shrouded male)"]
  J2 = shrouded pin header, 6 pins [form="♂ (shrouded male)"]
  J3 = shrouded pin header, 6 pins [form="♂ (shrouded male)"]
  J4 = shrouded pin header, 6 pins [form="♂ (shrouded male)"]
  J5 = shrouded pin header, 6 pins [form="♂ (shrouded male)"]
  J6 = shrouded pin header, 6 pins [form="♂ (shrouded male)"]
  J7 = shrouded pin header, 6 pins [form="♂ (shrouded male)"]
  J8 = shrouded pin header, 6 pins [form="♂ (shrouded male)"]
  J9 = shrouded pin header, 6 pins [form="♂ (shrouded male)"]
  J10 = shrouded pin header, 6 pins [form="♂ (shrouded male)"]
  J11 = shrouded pin header, 6 pins [form="♂ (shrouded male)"]
  J12 = shrouded pin header, 6 pins [form="♂ (shrouded male)"]
  J13 = shrouded pin header, 6 pins [form="♂ (shrouded male)"]
  J14 = shrouded pin header, 6 pins [form="♂ (shrouded male)"]
  J15 = shrouded pin header, 6 pins [form="♂ (shrouded male)"]
  J16 = shrouded pin header, 6 pins [form="♂ (shrouded male)"]
  J17 = shrouded pin header, 6 pins [form="♂ (shrouded male)"]
  J18 = shrouded pin header, 6 pins [form="♂ (shrouded male)"]
  J19 = shrouded pin header, 6 pins [form="♂ (shrouded male)"]
  J21 = shrouded pin header, 6 pins [form="♂ (shrouded male)"]
  J22 = Power Jack [package=power_jack_pth_lock]
  R2 = TRIMPOT [package=3362u-2]
  J20 = shrouded pin header, 6 pins [form="♂ (shrouded male)"]
  LED1 = LED - 3mm [color="Green (570nm)" package="3 mm [THT]"]
  LED2 = LED - 3mm [color="Green (570nm)" package="3 mm [THT]"]
  LED3 = LED - 3mm [color="Green (570nm)" package="3 mm [THT]"]
  LED4 = LED - 3mm [color="Green (570nm)" package="3 mm [THT]"]
  LED5 = LED - 3mm [color="Green (570nm)" package="3 mm [THT]"]
  LED6 = LED - 3mm [color="Green (570nm)" package="3 mm [THT]"]
  LED7 = LED - 3mm [color="Green (570nm)" package="3 mm [THT]"]
  LED8 = LED - 3mm [color="Green (570nm)" package="3 mm [THT]"]
  LED9 = LED - 3mm [color="Green (570nm)" package="3 mm [THT]"]
  LED10 = LED - 3mm [color="Green (570nm)" package="3 mm [THT]"]
  LED11 = LED - 3mm [color="Green (570nm)" package="3 mm [THT]"]
  LED12 = LED - 3mm [color="Green (570nm)" package="3 mm [THT]"]
  LED13 = LED - 3mm [color="Green (570nm)" package="3 mm [THT]"]
  LED15 = LED - 3mm [color="Green (570nm)" package="3 mm [THT]"]
  LED16 = LED - 3mm [color="Green (570nm)" package="3 mm [THT]"]
  LED17 = LED - 3mm [color="Green (570nm)" package="3 mm [THT]"]
  LED18 = LED - 3mm [color="Green (570nm)" package="3 mm [THT]"]
  LED19 = LED - 3mm [color="Green (570nm)" package="3 mm [THT]"]
  LED20 = LED - 3mm [color="Green (570nm)" package="3 mm [THT]"]
  LED14 = LED - 3mm [color="Green (570nm)" package="3 mm [THT]"]
  X1 = DB9 Connector [package=db9]
  J23 = female pin header, 2 pins [form="♀ (female)"]
  R3 = Resistor [tolerance=±5% resistance=220 package=THT]

nets:
  N1: PI.pin1, R3.Pin_1
  N2: PI.pin2, J19.pin4, LED10.anode
  N3: PI.pin3, J18.pin4, LED11.anode
  N4: PI.pin4, J15.pin4, LED12.anode
  N5: PI.pin6, J21.pin4, LED13.anode
  N6: PI.pin7, J20.pin4, LED14.anode
  N7: PI.pin8, J23.pin2, R3.Pin_0
  N8: PI.pin10, X1.5
  N9: PI.pin11, X1.4
  N10: PI.pin12, X1.3
  N11: PI.pin15, J2.pin4, LED19.anode
  N12: PI.pin16, J3.pin4, LED20.anode
  N13: PI.pin17, J4.pin4, LED18.anode
  N14: PI.pin18, J5.pin4, LED17.anode
  N15: PI.pin19, J7.pin4, LED16.anode
  N16: PI.pin21, J6.pin4, LED15.anode
  N17: PI.pin22, J8.pin4, LED6.anode
  N18: PI.pin23, J10.pin4, LED5.anode
  N19: PI.pin25, J9.pin4, LED1.anode
  N20: PI.pin28, X1.2
  N21: PI.pin29, X1.1
  N22: PI.pin30, J11.pin4, LED2.anode
  N23: PI.pin32, J14.pin4, LED3.anode
  N24: PI.pin33, J16.pin4, LED4.anode
  N25: PI.pin35, J13.pin4, LED7.anode
  N26: PI.pin36, J12.pin4, LED8.anode
  N27: PI.pin37, J17.pin4, LED9.anode
  N28: PI.pin38, J2.pin1, J3.pin1, J4.pin1, J5.pin1, J6.pin1, J7.pin1, J8.pin1, J9.pin1, J10.pin1, J11.pin1, J12.pin1, J13.pin1, J14.pin1, J15.pin1, J16.pin1, J17.pin1, J18.pin1, J19.pin1, J21.pin1, J22.GND, R2.CW, J20.pin1, LED1.cathode, LED2.cathode, LED3.cathode, LED4.cathode, LED5.cathode, LED6.cathode, LED7.cathode, LED8.cathode, LED9.cathode, LED10.cathode, LED11.cathode, LED12.cathode, LED13.cathode, LED15.cathode, LED16.cathode, LED17.cathode, LED18.cathode, LED19.cathode, LED20.cathode, LED14.cathode, X1.6, J23.pin1
  N29: J2.pin2, J2.pin5, J3.pin2, J3.pin5, J4.pin2, J4.pin5, J5.pin2, J5.pin5, J6.pin2, J6.pin5, J7.pin2, J7.pin5, J8.pin2, J8.pin5, J9.pin2, J9.pin5, J10.pin2, J10.pin5, J11.pin2, J11.pin5, J12.pin2, J12.pin5, J13.pin2, J13.pin5, J14.pin2, J14.pin5, J15.pin2, J15.pin5, J16.pin2, J16.pin5, J17.pin2, J17.pin5, J18.pin2, J18.pin5, J19.pin2, J19.pin5, J21.pin2, J21.pin5, R2.WIPER, J20.pin2, J20.pin5
  N30: J2.pin6, J3.pin6, J4.pin6, J5.pin6, J6.pin6, J7.pin6, J8.pin6, J9.pin6, J10.pin6, J11.pin6, J12.pin6, J13.pin6, J14.pin6, J15.pin6, J16.pin6, J17.pin6, J18.pin6, J19.pin6, J21.pin6, J22.PWR, R2.CCW, J20.pin6

notes:
  REF
  VCC 5V
  GND
  RASPBERRY PI B+
  GPIO 21
  GPIO 20
  GPIO 16
  GPIO 12
  GPIO 25
  GPIO 26
  GPIO 19
  GPIO 13
  GPIO 06
  GPIO 05
  GPIO 24
  GPIO 23
  GPIO 18
  GPIO 15
  GPIO 14
  UART0_RXD
  UART0_TXD
  GPIO 02
  GPIO 03
  GPIO 04
  GPIO 17
  GPIO 27
  SDA1_I2C
  SCL1_I2C
  PCM_CLK
  rev #02
  GPIO Breakout with REF Voltage
  SCLK / GPIO 11
  CE0 / GPIO 08
  CE1 / GPIO 07
  MISO / GPIO 09
  MOSI / GPIO 10
  GPIO 22
  RESET
  PULL-UP
